# Fritzing sketch test (saved by Fritzing 0.9.3b)
breadboards: 1

parts:
  Brushless_motor1 = Brushless Motor
  ESC1 = ESC 30A
  U2 = LIPO-11.1V-3 Cells [package=Li-Po-2200]
  Raspberry_Pi_1 = Raspberry Pi 3 [part_number=RPI-3-V1.2]
  LCD1 = LCD screen
  LCM1602_IIC1 = LCM1602 IIC [part_number="LCM1602 IIC" chip_label="LCM1602 IIC" package="DIP (Dual Inline) [THT]"]
  TCRT1 = TCRT5000 sensor module [part_number=151608]

nets:
  N1: Brushless_motor1.A, ESC1.A
  N2: Brushless_motor1.B, ESC1.B
  N3: Brushless_motor1.C, ESC1.C
  N4: ESC1.GND#4, ESC1.In, Raspberry_Pi_1.GND
  N5: ESC1.GND#5, U2.-
  N6: ESC1.V+, U2.+
  N7: Raspberry_Pi_1.GPIO2, LCM1602_IIC1.SDA
  N8: Raspberry_Pi_1.GIPO4, LCM1602_IIC1.SCL
  N9: Raspberry_Pi_1.GIPO21, LCM1602_IIC1.GND, TCRT1.T+
  5V: Raspberry_Pi_1.5V, LCM1602_IIC1.VCC, TCRT1.T-
  VSS: LCD1.VSS, LCM1602_IIC1.VSS
  VDD: LCD1.VDD, LCM1602_IIC1.VDD
  N10: LCD1.V0, LCM1602_IIC1.V0
  N11: LCD1.RS, LCM1602_IIC1.RS
  N12: LCD1.R/W, LCM1602_IIC1.RW
  N13: LCD1.E, LCM1602_IIC1.E
  N14: LCD1.DB0, LCM1602_IIC1.D0
  N15: LCD1.DB1, LCM1602_IIC1.D1
  N16: LCD1.DB2, LCM1602_IIC1.D2
  N17: LCD1.DB3, LCM1602_IIC1.D3
  N18: LCD1.DB4, LCM1602_IIC1.D4
  N19: LCD1.DB5, LCM1602_IIC1.D5
  N20: LCD1.DB6, LCM1602_IIC1.D6
  N21: LCD1.DB7, LCM1602_IIC1.D7
  N22: LCD1.LED+, LCM1602_IIC1.A
  N23: LCD1.LED-, LCM1602_IIC1.K
  N24: LCM1602_IIC1.LED_A, LCM1602_IIC1.LED_B

custom parts:
  Brushless Motor: A standard Brushless DC motor
  ESC 30A: Electronic Speed Controller - 30A
  LIPO-11.1V-3 Cells: Li-Po Battery-11.1V-3Cells-2200mAh
  LCM1602 IIC: I2C-Module to use a 1602 or 2004 LCD on with the wire.h libory Serial LCD Modul
  TCRT5000 sensor module: breakout board with TCRT5000
